# Fritzing sketch teensy2 (saved by Fritzing 0.9.3b)
circuit board: 7.5cm x 7.5cm
breadboards: 1

parts:
  J4 = female pin header, 2 pins [form="♀ (female)"]
  J6 = female pin header, 2 pins [form="♀ (female)"]
  J5 = male pin header, 12 pins [form="♂ (male)"]
  R1 = Resistor [tolerance=±5% resistance=220 package=THT]
  J8 = female pin header, 2 pins [form="♀ (female)"]
  J9 = female pin header, 3 pins [form="♀ (female)"]
  J3 = screw terminal, 2 pins
  J7 = screw terminal, 2 pins
  IC1 = IC, DIP package, 18 pins [chip_label=74c922]
  J10 = male pin header, 8 pins [form="♂ (male)"]
  C1 = Ceramic Capacitor [capacitance=10µF package="100 mil [THT, multilayer]"]
  C2 = Ceramic Capacitor [capacitance=100nF package="100 mil [THT, multilayer]"]
  Teensy_2 = Teensy 2.0
  J11 = female pin header, 4 pins [form="♀ (female)"]
  J12 = female pin header, 2 pins [form="♀ (female)"]
  J13 = female pin header, 1 pin [form="♀ (female)"]
  J1 = screw terminal, 12 pins

nets:
  N1: J4.pin1, J8.pin1, J3.pin2
  N2: J4.pin2, J9.pin1, J3.pin1
  N3: J6.pin1, R1.Pin_1, J7.pin2
  N4: J6.pin2, J7.pin1, Teensy_2.B1
  N5: J5.pin1, Teensy_2.B2, J1.pin12
  N6: J5.pin2, Teensy_2.B3, J1.pin11
  N7: J5.pin3, Teensy_2.B7, J1.pin10
  N8: J5.pin4, Teensy_2.D0, J1.pin9
  N9: J5.pin5, Teensy_2.D1, J1.pin8
  N10: J5.pin6, Teensy_2.D2, J1.pin7
  N11: J5.pin7, Teensy_2.D3, J1.pin6
  N12: J5.pin8, Teensy_2.C6, J1.pin5
  N13: J5.pin9, Teensy_2.C7, J1.pin4
  N14: J5.pin10, IC1.pin18, Teensy_2.VCC, J1.pin3
  N15: J5.pin11, J5.pin12, R1.Pin_0, J9.pin2, IC1.pin9, IC1.pin13, C1.0, C2.1, Teensy_2.GND, J11.pin4, J1.pin1, J1.pin2
  N16: J8.pin2, J9.pin3, Teensy_2.B0
  N17: IC1.pin1, J10.pin8
  N18: IC1.pin2, J10.pin7
  N19: IC1.pin3, J10.pin6
  N20: IC1.pin4, J10.pin5
  N21: IC1.pin5, C2.0
  N22: IC1.pin6, C1.1
  N23: IC1.pin7, J10.pin4
  N24: IC1.pin8, J10.pin3
  N25: IC1.pin10, J10.pin2
  N26: IC1.pin11, J10.pin1
  N27: IC1.pin12, Teensy_2.F5
  N28: IC1.pin14, Teensy_2.F7
  N29: IC1.pin15, Teensy_2.B6
  N30: IC1.pin16, Teensy_2.B5
  N31: IC1.pin17, Teensy_2.B4
  N32: Teensy_2.D6, J12.pin1
  N33: Teensy_2.D7, J12.pin2
  N34: Teensy_2.F6, J13.pin1
  N35: Teensy_2.F4, J11.pin1
  N36: Teensy_2.F1, J11.pin2
  N37: Teensy_2.F0, J11.pin3

notes:
  Encoder A
  X
  Y
  Z
  A
  X1
  X10
  X100
  COM
  +5v
  Gnd
  Encoder B
  Vcc
  ESTOP
  LED
